// Logisim project adder1bit.circ as structural Verilog: 2 circuits, main circuit main
module main (
  input  A,
  input  B,
  input  Cin,
  output S,
  output Cout
);

  wire and_1_out, and_2_out, xor_1_out;

  xor xor_1 (xor_1_out, A, B);
  xor xor_2 (S, xor_1_out, Cin);
  and and_1 (and_1_out, xor_1_out, Cin);
  and and_2 (and_2_out, A, B);
  or or_1 (Cout, and_1_out, and_2_out);
endmodule

module adder4bit (
  input  [3:0] A,
  input  [3:0] B,
  input  Cin,
  output Cout,
  output [3:0] S
);

  wire main_2_cout, main_3_cout, main_4_cout;

  main main_1 (.B(B[3]), .Cin(main_2_cout), .A(A[3]), .S(S[3]), .Cout(Cout));
  main main_2 (.B(B[2]), .Cin(main_3_cout), .A(A[2]), .S(S[2]), .Cout(main_2_cout));
  main main_3 (.B(B[1]), .Cin(main_4_cout), .A(A[1]), .S(S[1]), .Cout(main_3_cout));
  main main_4 (.B(B[0]), .Cin(Cin), .A(A[0]), .S(S[0]), .Cout(main_4_cout));
endmodule
